# Fritzing sketch Cube Solver (saved by Fritzing 0.8.0b)

parts:
  Arduino1 = Arduino
  J1 = Basic Servo
  J2 = Basic Servo

nets:
  N1: Arduino1.D9, J2.pulse
  N2: Arduino1.D6, J1.pulse
  3V3: Arduino1.3V3, J2.vcc
  +5V: Arduino1.+5V, J1.vcc
  GND: Arduino1.GND, J1.gnd, J2.gnd

notes:
  Rotate Servo - Pin 9
  Push Servo - Pin 6
